// Logisim project alu.circ as structural Verilog: 1 circuit, main circuit alu
module alu (
  input  [31:0] A,
  input  [31:0] B,
  input  [3:0] ALUSel,
  output [31:0] Result
);

  wire comparator_1_lt, mul_select;
  wire [31:0] a_abs, add0, and1, b_abs, divu8, mul10, mulh14, mulhu11, multiplier_3_cout, negator_1_out,
       not_1_out, not_2_out, or2, remu9, sll6, slt7, sra5, srl4, sub12, subtractor_2_out, xor3;

  Multiplexer #(.select(4), .width(32), .enable("false")) multiplexer_1 (
    .in0(add0), .in1(and1), .in2(or2), .in3(xor3), .in4(srl4), .in5(sra5), .in6(sll6), .in7(slt7),
    .in8(divu8), .in9(remu9), .in10(mul10), .in11(mulhu11), .in12(sub12), .in13(B), .in14(mulh14),
    .out(Result), .sel(ALUSel));  // open: in15
  Adder #(.width(32)) adder_1 (.a(A), .b(B), .out(add0));  // open: cin, cout
  assign and1 = A & B;  // AND_Gate and_1, 32 bits wide
  assign or2 = A | B;  // OR_Gate or_1, 32 bits wide
  assign xor3 = A ^ B;  // XOR_Gate xor_1, 32 bits wide
  Shifter #(.width(32), .shift("lr")) shifter_1 (.in(A), .\dist (B[4:0]), .out(srl4));
  Shifter #(.width(32)) shifter_2 (.in(A), .\dist (B[4:0]), .out(sll6));
  Multiplier #(.width(32)) multiplier_1 (.a(A), .b(B), .cout(mulhu11));  // open: out, cin
  Shifter #(.width(32), .shift("ar")) shifter_3 (.in(A), .\dist (B[4:0]), .out(sra5));
  Comparator #(.width(32)) comparator_1 (.a(A), .b(B), .lt(comparator_1_lt));  // open: gt, eq
  Divider #(.width(32)) divider_1 (.a(A), .b(B), .out(divu8));  // open: upper, rem
  Divider #(.width(32)) divider_2 (.a(A), .b(B), .rem(remu9));  // open: out, upper
  Multiplier #(.width(32)) multiplier_2 (.a(A), .b(B), .out(mul10));  // open: cin, cout
  assign slt7 = {{31{1'b0}}, comparator_1_lt};  // Bit_Extender bit_extender_1
  Multiplexer #(.width(32), .enable("false")) multiplexer_2 (.in0(A), .in1(not_1_out), .out(a_abs), .sel(A[31]));
  assign not_1_out = ~A;  // NOT_Gate not_1, 32 bits wide
  Multiplexer #(.width(32), .enable("false")) multiplexer_3 (.in0(B), .in1(not_2_out), .out(b_abs), .sel(B[31]));
  assign not_2_out = ~B;  // NOT_Gate not_2, 32 bits wide
  Subtractor #(.width(32)) subtractor_1 (.a(A), .b(B), .out(sub12));  // open: bin, bout
  Negator #(.width(32)) negator_1 (.in(multiplier_3_cout), .out(negator_1_out));
  xnor xnor_1 (mul_select, A[31], B[31]);
  Subtractor #(.width(32)) subtractor_2 (.a(negator_1_out), .b(32'h1), .out(subtractor_2_out));  // open: bin, bout
  Multiplier #(.width(32)) multiplier_3 (.a(a_abs), .b(b_abs), .cout(multiplier_3_cout));  // open: out, cin
  Multiplexer #(.width(32), .enable("false")) multiplexer_4 (
    .in0(subtractor_2_out), .in1(multiplier_3_cout), .out(mulh14), .sel(mul_select));

  // Other names for the same wires on the sheet: a_rest[30:0] = A[30:0]; a_bit = A[31]; b_rest[30:0] = B[30:0];
  //   bsel13[31:0] = B; b_bit = B[31]

  // Notes on the sheet:
  //   INPUTS to your circuit
  //   Srl
  //   Sll
  //   Adder
  //   Xor
  //   And
  //   Or
  //   DON'T CHANGE THE LOCATIONS OF THE INPUTS AND OUTPUTS!
  //   Sra
  //   Slt
  //   Divu
  //   Remu
  //   Mul
  //   Mulhu
  //   Sub
  //   Bsel
  //   OUTPUT from your circuit
endmodule
