// Logisim project control.circ as structural Verilog: 2 circuits, main circuit main
module main (
  input  [31:0] INSTRUCTION,
  input  CLOCK,
  output [31:0] PROGRAM_COUNTER,
  output [31:0] ra,
  output [31:0] sp,
  output [31:0] t0,
  output [31:0] t1,
  output [31:0] t2,
  output [31:0] s0,
  output [31:0] s1,
  output [31:0] a0
);

  wire DMEM_p1, DMEM_p3;
  wire [31:0] adder_1_out, Arithmetic_Logic_Unit_result, bit_extender_1_out, RegFile_read_data_1,
       register_1_q;

  Register #(.width(32)) PC (.D(adder_1_out), .clk(CLOCK), .Q(PROGRAM_COUNTER));  // open: en, clr
  Adder #(.width(32)) adder_1 (.a(PROGRAM_COUNTER), .b(32'h4), .out(adder_1_out));  // open: cin, cout
  Register #(.width(32)) register_1 (.clk(CLOCK), .Q(register_1_q));  // open: D, en, clr
  assign bit_extender_1_out = {{20{register_1_q[31]}}, register_1_q[31:20]};  // Bit_Extender bit_extender_1
  regfile_main RegFile (
    .rd(register_1_q[11:7]), .Read_Data_1(RegFile_read_data_1), .ra(ra), .sp(sp), .t0(t0), .t1(t1), .t2(t2),
    .s0(s0), .s1(s1), .a0(a0), .rs1(register_1_q[19:15]), .Write_Data(Arithmetic_Logic_Unit_result),
    .RegWEn(1'b1), .clk(CLOCK));  // open: rs2, Read_Data_2
  alu Arithmetic_Logic_Unit (
    .B(bit_extender_1_out), .Result(Arithmetic_Logic_Unit_result), .A(RegFile_read_data_1), .ALUSel(4'b0000));
  // mem_main DMEM: pin names not known; wires that end beside it: DMEM_p1, DMEM_p1, DMEM_p3

  // Other names for the same wires on the sheet: clk = CLOCK

  // Notes on the sheet:
  //   Output
  //   IMEM (do **NOT** move this)
  //   Inputs
  //   Inputs/Outputs for testing. Do **NOT** move these.
endmodule

module control (
);

  wire adder_9_cout, first_b, func7_1r, func7_5r, func7_7r, mulhu, or_r, x_or;
  wire [1:0] func7_0r;
  wire [3:0] ALUSel_add, ALUSel_and, ALUSel_divu, ALUSel_mul, ALUSel_mulh, ALUSel_mulhu, ALUSel_or,
       ALUSel_remu, ALUSel_sll, ALUSel_srl, ALUSel_sub, ALUSel_xor, b_four_b, demultiplexer_4_out1,
       demultiplexer_4_out2, demultiplexer_5_out0, demultiplexer_5_out1, demultiplexer_6_out0,
       demultiplexer_6_out1, demultiplexer_7_out1, demultiplexer_8_out0, demultiplexer_9_out0,
       demultiplexer_9_out1, demultiplexer_10_out0, form_sel;
  wire [5:0] demultiplexer_3_out1, demultiplexer_3_out3, demultiplexer_3_out4, demultiplexer_3_out5,
       demultiplexer_3_out6, demultiplexer_3_out7;
  wire [5:1] demultiplexer_3_out0;
  wire [6:0] slt;
  wire [31:0] i, i_loads, jalr, r, r_or_u, s, sb, u, uj;
  wire [31:4] INSTRUCTION;

  Multiplexer #(.width(4), .enable("false")) multiplexer_1 (
    .in0({first_b, INSTRUCTION[5:4], b_four_b[3]}), .in1(b_four_b), .out(form_sel), .sel(first_b));
  Demultiplexer #(.select(4), .width(32), .enable("false")) demultiplexer_1 (
    .out0(i_loads), .out2(i), .out3(sb), .out4(s), .out6(r_or_u), .out7(jalr), .out14(uj),
    .in({INSTRUCTION[31:7], first_b, INSTRUCTION[5:4], b_four_b}), .sel(form_sel));  // open: out1, out5, out8, out9, out10, out11, out12, out13, out15
  Demultiplexer #(.select(4), .width(32), .enable("false")) demultiplexer_2 (
    .out2(r), .out6(u), .in(r_or_u), .sel(b_four_b));  // open: out0, out1, out3, out4, out5, out7, out8, out9, out10, out11, out12, out13, out14, out15
  Demultiplexer #(.select(3), .width(7), .enable("false")) demultiplexer_3 (
    .out0({func7_0r[1], demultiplexer_3_out0, func7_0r[0]}), .out1({func7_1r, demultiplexer_3_out1}),
    .out2(slt), .out3({mulhu, demultiplexer_3_out3}), .out4({x_or, demultiplexer_3_out4}),
    .out5({func7_5r, demultiplexer_3_out5}), .out6({or_r, demultiplexer_3_out6}),
    .out7({func7_7r, demultiplexer_3_out7}), .in(r[31:25]), .sel(r[14:12]));
  Demultiplexer #(.select(2), .width(4), .enable("false")) demultiplexer_4 (
    .out0(ALUSel_add), .out1(demultiplexer_4_out1), .out2(demultiplexer_4_out2), .in(4'b0000), .sel(func7_0r));  // open: out3
  Demultiplexer #(.width(4), .enable("false")) demultiplexer_5 (
    .out0(demultiplexer_5_out0), .out1(demultiplexer_5_out1), .in(4'b0000), .sel(func7_7r));
  Demultiplexer #(.width(4), .enable("false")) demultiplexer_6 (
    .out0(demultiplexer_6_out0), .out1(demultiplexer_6_out1), .in(4'b0000), .sel(func7_1r));
  Demultiplexer #(.width(4), .enable("false")) demultiplexer_7 (
    .out1(demultiplexer_7_out1), .in(4'b0000), .sel(mulhu));  // open: out0
  Adder #(.width(4)) adder_1 (.a(4'b0001), .b(demultiplexer_5_out0), .out(ALUSel_and));  // open: cin, cout
  Adder #(.width(4)) adder_2 (.a(demultiplexer_5_out1), .b(4'b1001), .out(ALUSel_remu));  // open: cin, cout
  Adder #(.width(4)) adder_3 (.a(demultiplexer_4_out1), .b(4'b1010), .out(ALUSel_mul));  // open: cin, cout
  Adder #(.width(4)) adder_4 (.a(demultiplexer_4_out2), .b(4'b1100), .out(ALUSel_sub));  // open: cin, cout
  Adder #(.width(4)) adder_5 (.a(4'b0110), .b(demultiplexer_6_out0), .out(ALUSel_sll));  // open: cin, cout
  Adder #(.width(4)) adder_6 (.a(demultiplexer_6_out1), .b(4'b1110), .out(ALUSel_mulh));  // open: cin, cout
  Adder #(.width(4)) adder_7 (.a(4'b1011), .b(demultiplexer_7_out1), .out(ALUSel_mulhu));  // open: cin, cout
  Demultiplexer #(.width(4), .enable("false")) demultiplexer_8 (
    .out0(demultiplexer_8_out0), .in(4'b0000), .sel(x_or));  // open: out1
  Demultiplexer #(.width(4), .enable("false")) demultiplexer_9 (
    .out0(demultiplexer_9_out0), .out1(demultiplexer_9_out1), .in(4'b0000), .sel(func7_5r));
  Adder #(.width(4)) adder_8 (.a(4'b0011), .b(demultiplexer_8_out0), .out(ALUSel_xor));  // open: cin, cout
  Adder #(.width(4)) adder_9 (
    .a(4'b0100), .b(demultiplexer_9_out0), .out(ALUSel_srl), .cout(adder_9_cout));  // open: cin
  Adder #(.width(4)) adder_10 (
    .a(demultiplexer_9_out1), .b(4'b1000), .out(ALUSel_divu), .cin(adder_9_cout));  // open: cout
  Demultiplexer #(.width(4), .enable("false")) demultiplexer_10 (
    .out0(demultiplexer_10_out0), .in(4'b0000), .sel(or_r));  // open: out1
  Adder #(.width(4)) adder_11 (.a(demultiplexer_10_out0), .b(4'b0010), .out(ALUSel_or));  // open: cin, cout

  // Other names for the same wires on the sheet: INSTRUCTION (some bits) = {first_b, b_four_b};
  //   t_four_b[3:0] = {first_b, INSTRUCTION[5:4], b_four_b[3]}; r_func3[2:0] = r[14:12]; r_func7[6:0] = r[31:25]
endmodule
