// Logisim project cpu.circ as structural Verilog: 5 circuits, main circuit main
module main (
  input  [31:0] INSTRUCTION,
  input  CLOCK,
  output [31:0] PROGRAM_COUNTER,
  output [31:0] ra,
  output [31:0] sp,
  output [31:0] t0,
  output [31:0] t1,
  output [31:0] t2,
  output [31:0] s0,
  output [31:0] s1,
  output [31:0] a0
);

  wire ASel, BrEq, BrLT, BrUn, BSel, DMEM_p1, DMEM_p6, MemRW, PCSel, RegWEn;
  wire [1:0] WBSel;
  wire [2:0] ImmSel;
  wire [3:0] ALUSel;
  wire [4:0] instruction_mem_1_rd, instruction_mem_1_rs1, instruction_mem_1_rs2;
  wire [31:0] adder_1_out, adder_2_out, Arithmetic_Logic_Unit_result, DMEM_p8, imm, INSTRUCTION_t,
       multiplexer_1_out, multiplexer_3_out, multiplexer_4_out, RegFile_read_data_1, RegFile_read_data_2,
       register_1_q, register_2_q, wb;

  Adder #(.width(32)) adder_1 (.a(PROGRAM_COUNTER), .b(32'h4), .out(adder_1_out));  // open: cin, cout
  Register #(.width(32)) PC (.D(multiplexer_1_out), .clk(CLOCK), .Q(PROGRAM_COUNTER));  // open: en, clr
  Multiplexer #(.width(32), .enable("false")) multiplexer_1 (
    .in0(adder_1_out), .in1(Arithmetic_Logic_Unit_result), .out(multiplexer_1_out), .sel(PCSel));
  Register #(.width(32)) register_1 (.D(PROGRAM_COUNTER), .clk(CLOCK), .Q(register_1_q));  // open: en, clr
  Register #(.width(32)) register_2 (.D(INSTRUCTION_t), .clk(CLOCK), .Q(register_2_q));  // open: en, clr
  control control_1 (
    .INSTRUCTION(register_2_q), .BrEq(BrEq), .BrLt(BrLT), .BrUn(BrUn), .WBSel(WBSel), .MemRW(MemRW),
    .ASel(ASel), .BSel(BSel), .ImmSel(ImmSel), .RegWEn(RegWEn), .PCSel(PCSel), .ALUSel(ALUSel));
  Instruction_Mem instruction_mem_1 (
    .INSTRUCTION(register_2_q), .rs1(instruction_mem_1_rs1), .rd(instruction_mem_1_rd),
    .rs2(instruction_mem_1_rs2));
  Multiplexer #(.width(32), .enable("false")) multiplexer_2 (
    .in0(INSTRUCTION), .in1(32'h13), .out(INSTRUCTION_t), .sel(PCSel));
  ImmGen immgen_1 (.instruction(register_2_q), .ImmSel(ImmSel), .immediate(imm));
  regfile_main RegFile (
    .rs2(instruction_mem_1_rs2), .rd(instruction_mem_1_rd), .Read_Data_1(RegFile_read_data_1),
    .Read_Data_2(RegFile_read_data_2), .ra(ra), .sp(sp), .t0(t0), .t1(t1), .t2(t2), .s0(s0), .s1(s1),
    .a0(a0), .rs1(instruction_mem_1_rs1), .Write_Data(wb), .RegWEn(RegWEn), .clk(CLOCK));
  BranchComp branchcomp_1 (.rs1(RegFile_read_data_1), .rs2(RegFile_read_data_2), .BrUn(BrUn), .BrEq(BrEq), .BrLT(BrLT));
  Multiplexer #(.width(32), .enable("false")) multiplexer_3 (
    .in0(register_1_q), .in1(RegFile_read_data_1), .out(multiplexer_3_out), .sel(ASel));
  Multiplexer #(.width(32), .enable("false")) multiplexer_4 (
    .in0(RegFile_read_data_2), .in1(imm), .out(multiplexer_4_out), .sel(BSel));
  alu Arithmetic_Logic_Unit (
    .B(multiplexer_4_out), .Result(Arithmetic_Logic_Unit_result), .A(multiplexer_3_out), .ALUSel(ALUSel));
  Adder #(.width(32)) adder_2 (.a(register_1_q), .b(32'h4), .out(adder_2_out));  // open: cin, cout
  Multiplexer #(.select(2), .width(32), .enable("false")) multiplexer_5 (
    .in0(adder_2_out), .in1(Arithmetic_Logic_Unit_result), .in2(DMEM_p8), .out(wb), .sel(WBSel));  // open: in3
  // mem_main DMEM: pin names not known; wires that end beside it: DMEM_p1, Arithmetic_Logic_Unit_result, RegFile_read_data_2, DMEM_p1, CLOCK, DMEM_p6, MemRW, DMEM_p8

  // Other names for the same wires on the sheet: clk = CLOCK

  // Notes on the sheet:
  //   Output
  //   IMEM (do **NOT** move this)
  //   Inputs
  //   Inputs/Outputs for testing. Do **NOT** move these.
endmodule

module control (
  input  [31:0] INSTRUCTION,
  input  BrEq,
  input  BrLt,
  output BrUn,
  output [1:0] WBSel,
  output MemRW,
  output ASel,
  output BSel,
  output [2:0] ImmSel,
  output RegWEn,
  output PCSel,
  output [3:0] ALUSel
);

  wire adder_9_cout, adder_15_cout, func7_1r, func7_5r, func7_7r, i_imms, i_loader, mulhu, multiplexer_7_out,
       not_1_out, or_r, sb_PCSel, slt, x_or;
  wire [1:0] func7_0r;
  wire [3:0] ALUSel_add_i, ALUSel_add_r, ALUSel_and_i, ALUSel_and_r, ALUSel_divu_r, ALUSel_I, ALUSel_mul_r,
       ALUSel_mulh_r, ALUSel_mulhu_r, ALUSel_or_i, ALUSel_or_r, ALUSel_R, ALUSel_remu_r, ALUSel_sll_i,
       ALUSel_sll_r, ALUSel_slt_i, ALUSel_slt_r, ALUSel_sra_i, ALUSel_srl_i, ALUSel_srl_r, ALUSel_sub_r,
       ALUSel_xor_i, ALUSel_xor_r, demultiplexer_4_out1, demultiplexer_4_out2, demultiplexer_5_out0,
       demultiplexer_5_out1, demultiplexer_6_out0, demultiplexer_6_out1, demultiplexer_7_out1,
       demultiplexer_8_out0, demultiplexer_9_out0, demultiplexer_9_out1, demultiplexer_10_out0,
       demultiplexer_11_out0, demultiplexer_13_out1, demultiplexer_13_out2, demultiplexer_13_out4,
       demultiplexer_13_out5, demultiplexer_13_out6, demultiplexer_13_out7, demultiplexer_14_out0,
       demultiplexer_14_out1, form_sel, multiplexer_12_out;
  wire [5:0] demultiplexer_3_out1, demultiplexer_3_out2, demultiplexer_3_out3, demultiplexer_3_out4,
       demultiplexer_3_out5, demultiplexer_3_out6, demultiplexer_3_out7;
  wire [5:1] demultiplexer_3_out0;
  wire [31:0] i, i_loads, jalr, r, r_or_u, s, sb, u, uj;

  Multiplexer #(.width(4), .enable("false")) multiplexer_1 (
    .in0(INSTRUCTION[6:3]), .in1(INSTRUCTION[3:0]), .out(form_sel), .sel(INSTRUCTION[6]));
  Multiplexer #(.select(4), .width(4), .enable("false")) multiplexer_2 (
    .in0(4'b0000), .in2(ALUSel_I), .in3(4'b0000), .in4(4'b0000), .in6(ALUSel_R), .in7(4'b0000),
    .in15(4'b0000), .out(ALUSel), .sel(form_sel));  // open: in1, in5, in8, in9, in10, in11, in12, in13, in14
  Demultiplexer #(.select(4), .width(32), .enable("false")) demultiplexer_1 (
    .out0(i_loads), .out2(i), .out3(sb), .out4(s), .out6(r_or_u), .out7(jalr), .out15(uj), .in(INSTRUCTION),
    .sel(form_sel));  // open: out1, out5, out8, out9, out10, out11, out12, out13, out14
  Multiplexer #(.select(5), .width(4), .enable("false")) multiplexer_3 (
    .in0(ALUSel_add_r), .in1(ALUSel_mul_r), .in2(ALUSel_sub_r), .in4(ALUSel_sll_r), .in5(ALUSel_mulh_r),
    .in8(ALUSel_slt_r), .in13(ALUSel_mulhu_r), .in16(ALUSel_xor_r), .in20(ALUSel_srl_r),
    .in21(ALUSel_divu_r), .in22(ALUSel_or_r), .in28(ALUSel_and_r), .in29(ALUSel_remu_r), .out(ALUSel_R),
    .sel({r[14:12], r[30], r[25]}));  // open: in3, in6, in7, in9, in10, in11, in12, in14, in15, in17, in18, in19, in23, in24, in25, in26, in27, in30, in31
  Multiplexer #(.select(4), .enable("false")) multiplexer_4 (
    .in0(1'b0), .in2(1'b0), .in3(sb_PCSel), .in4(1'b0), .in6(1'b0), .in7(1'b1), .in15(1'b1), .out(PCSel),
    .sel(form_sel));  // open: in1, in5, in8, in9, in10, in11, in12, in13, in14
  Multiplexer #(.select(4), .enable("false")) multiplexer_5 (
    .in0(1'b1), .in2(1'b1), .in3(1'b0), .in4(1'b0), .in6(1'b1), .in7(1'b1), .in15(1'b1), .out(RegWEn),
    .sel(form_sel));  // open: in1, in5, in8, in9, in10, in11, in12, in13, in14
  Demultiplexer #(.select(4), .width(32), .enable("false")) demultiplexer_2 (
    .out3(r), .out7(u), .in(r_or_u), .sel(INSTRUCTION[3:0]));  // open: out0, out1, out2, out4, out5, out6, out8, out9, out10, out11, out12, out13, out14, out15
  Demultiplexer #(.select(3), .width(7), .enable("false")) demultiplexer_3 (
    .out0({func7_0r[1], demultiplexer_3_out0, func7_0r[0]}), .out1({func7_1r, demultiplexer_3_out1}),
    .out2({slt, demultiplexer_3_out2}), .out3({mulhu, demultiplexer_3_out3}),
    .out4({x_or, demultiplexer_3_out4}), .out5({func7_5r, demultiplexer_3_out5}),
    .out6({or_r, demultiplexer_3_out6}), .out7({func7_7r, demultiplexer_3_out7}), .in(r[31:25]),
    .sel(r[14:12]));
  Multiplexer #(.select(4), .width(3), .enable("false")) multiplexer_6 (
    .in0(3'b000), .in2(3'b000), .in3(3'b010), .in4(3'b001), .in6(3'b011), .in7(3'b000), .in15(3'b100),
    .out(ImmSel), .sel(form_sel));  // open: in1, in5, in8, in9, in10, in11, in12, in13, in14
  Demultiplexer #(.select(2), .width(4), .enable("false")) demultiplexer_4 (
    .out0(ALUSel_add_r), .out1(demultiplexer_4_out1), .out2(demultiplexer_4_out2), .in(4'b0000),
    .sel(func7_0r));  // open: out3
  Demultiplexer #(.width(4), .enable("false")) demultiplexer_5 (
    .out0(demultiplexer_5_out0), .out1(demultiplexer_5_out1), .in(4'b0000), .sel(func7_7r));
  Multiplexer #(.select(4), .enable("false")) multiplexer_7 (
    .in3(1'b0), .in7(1'b1), .out(multiplexer_7_out), .sel(INSTRUCTION[3:0]));  // open: in0, in1, in2, in4, in5, in6, in8, in9, in10, in11, in12, in13, in14, in15
  Demultiplexer #(.width(4), .enable("false")) demultiplexer_6 (
    .out0(demultiplexer_6_out0), .out1(demultiplexer_6_out1), .in(4'b0000), .sel(func7_1r));
  Demultiplexer #(.width(4), .enable("false")) demultiplexer_7 (
    .out1(demultiplexer_7_out1), .in(4'b0000), .sel(mulhu));  // open: out0
  Adder #(.width(4)) adder_1 (.a(4'b0001), .b(demultiplexer_5_out0), .out(ALUSel_and_r));  // open: cin, cout
  Adder #(.width(4)) adder_2 (.a(demultiplexer_5_out1), .b(4'b1001), .out(ALUSel_remu_r));  // open: cin, cout
  Adder #(.width(4)) adder_3 (.a(demultiplexer_4_out1), .b(4'b1010), .out(ALUSel_mul_r));  // open: cin, cout
  Adder #(.width(4)) adder_4 (.a(demultiplexer_4_out2), .b(4'b1100), .out(ALUSel_sub_r));  // open: cin, cout
  Adder #(.width(4)) adder_5 (.a(4'b0110), .b(demultiplexer_6_out0), .out(ALUSel_sll_r));  // open: cin, cout
  Adder #(.width(4)) adder_6 (.a(demultiplexer_6_out1), .b(4'b1110), .out(ALUSel_mulh_r));  // open: cin, cout
  Adder #(.width(4)) adder_7 (.a(4'b1011), .b(demultiplexer_7_out1), .out(ALUSel_mulhu_r));  // open: cin, cout
  Demultiplexer #(.width(4), .enable("false")) demultiplexer_8 (
    .out0(demultiplexer_8_out0), .in(4'b0000), .sel(x_or));  // open: out1
  Demultiplexer #(.width(4), .enable("false")) demultiplexer_9 (
    .out0(demultiplexer_9_out0), .out1(demultiplexer_9_out1), .in(4'b0000), .sel(func7_5r));
  Multiplexer #(.select(4), .enable("false")) multiplexer_8 (
    .in0(1'b1), .in2(1'b1), .in3(1'b1), .in4(1'b1), .in6(multiplexer_7_out), .in7(1'b1), .in15(1'b1),
    .out(BSel), .sel(form_sel));  // open: in1, in5, in8, in9, in10, in11, in12, in13, in14
  Adder #(.width(4)) adder_8 (.a(4'b0011), .b(demultiplexer_8_out0), .out(ALUSel_xor_r));  // open: cin, cout
  Adder #(.width(4)) adder_9 (
    .a(4'b0100), .b(demultiplexer_9_out0), .out(ALUSel_srl_r), .cout(adder_9_cout));  // open: cin
  Adder #(.width(4)) adder_10 (
    .a(demultiplexer_9_out1), .b(4'b1000), .out(ALUSel_divu_r), .cin(adder_9_cout));  // open: cout
  Demultiplexer #(.width(4), .enable("false")) demultiplexer_10 (
    .out0(demultiplexer_10_out0), .in(4'b0000), .sel(or_r));  // open: out1
  Adder #(.width(4)) adder_11 (.a(demultiplexer_10_out0), .b(4'b0010), .out(ALUSel_or_r));  // open: cin, cout
  Demultiplexer #(.width(4), .enable("false")) demultiplexer_11 (
    .out0(demultiplexer_11_out0), .in(4'b0000), .sel(slt));  // open: out1
  Demultiplexer #(.enable("false")) demultiplexer_12 (.out0(i_loader), .out1(i_imms), .in(1'b1), .sel(i[4]));
  Multiplexer #(.select(4), .enable("false")) multiplexer_9 (
    .in0(1'b1), .in2(1'b1), .in3(1'b0), .in4(1'b1), .in6(1'b1), .in7(1'b1), .in15(1'b0), .out(ASel),
    .sel(form_sel));  // open: in1, in5, in8, in9, in10, in11, in12, in13, in14
  Adder #(.width(4)) adder_12 (.a(4'b0111), .b(demultiplexer_11_out0), .out(ALUSel_slt_r));  // open: cin, cout
  Multiplexer #(.select(3), .enable("false")) multiplexer_10 (
    .in4(1'b0), .in6(1'b1), .out(BrUn), .sel(sb[14:12]));  // open: in0, in1, in2, in3, in5, in7
  Demultiplexer #(.select(3), .width(4), .enable("false")) demultiplexer_13 (
    .out0(ALUSel_add_i), .out1(demultiplexer_13_out1), .out2(demultiplexer_13_out2),
    .out4(demultiplexer_13_out4), .out5(demultiplexer_13_out5), .out6(demultiplexer_13_out6),
    .out7(demultiplexer_13_out7), .in(4'b0000), .sel(i[14:12]));  // open: out3
  Multiplexer #(.select(4), .enable("false")) multiplexer_11 (
    .in0(1'b0), .in2(1'b0), .in3(1'b0), .in4(1'b1), .in6(1'b0), .in7(1'b0), .in15(1'b0), .out(MemRW),
    .sel(form_sel));  // open: in1, in5, in8, in9, in10, in11, in12, in13, in14
  Multiplexer #(.width(4), .enable("false")) multiplexer_12 (
    .in0(ALUSel_srl_i), .in1(ALUSel_sra_i), .out(multiplexer_12_out), .sel(i[30]));
  Demultiplexer #(.width(4), .enable("false")) demultiplexer_14 (
    .out0(demultiplexer_14_out0), .out1(demultiplexer_14_out1), .in(demultiplexer_13_out5), .sel(i[30]));
  not not_1 (not_1_out, BrEq);
  Adder #(.width(4)) adder_13 (.a(4'b0110), .b(demultiplexer_13_out1), .out(ALUSel_sll_i));  // open: cin, cout
  Adder #(.width(4)) adder_14 (.a(4'b0111), .b(demultiplexer_13_out2), .out(ALUSel_slt_i));  // open: cin, cout
  Multiplexer #(.select(3), .enable("false")) multiplexer_13 (
    .in0(BrEq), .in1(not_1_out), .in4(BrLt), .in6(BrLt), .out(sb_PCSel), .sel(sb[14:12]));  // open: in2, in3, in5, in7
  Adder #(.width(4)) adder_15 (
    .a(4'b0011), .b(demultiplexer_13_out4), .out(ALUSel_xor_i), .cout(adder_15_cout));  // open: cin
  Adder #(.width(4)) adder_16 (
    .a(4'b0100), .b(demultiplexer_14_out0), .out(ALUSel_srl_i), .cin(adder_15_cout));  // open: cout
  Adder #(.width(4)) adder_17 (.a(4'b0101), .b(demultiplexer_14_out1), .out(ALUSel_sra_i));  // open: cin, cout
  Adder #(.width(4)) adder_18 (.a(4'b0010), .b(demultiplexer_13_out6), .out(ALUSel_or_i));  // open: cin, cout
  Adder #(.width(4)) adder_19 (.a(demultiplexer_13_out7), .b(4'b0001), .out(ALUSel_and_i));  // open: cin, cout
  Multiplexer #(.select(4), .width(2), .enable("false")) multiplexer_14 (
    .in0(2'b10), .in2(2'b01), .in6(2'b01), .in7(2'b00), .in15(2'b00), .out(WBSel), .sel(form_sel));  // open: in1, in3, in4, in5, in8, in9, in10, in11, in12, in13, in14
  Multiplexer #(.select(4), .width(4), .enable("false")) multiplexer_15 (
    .in8(ALUSel_add_i), .in9(ALUSel_sll_i), .in10(ALUSel_slt_i), .in12(ALUSel_xor_i),
    .in13(multiplexer_12_out), .in14(ALUSel_or_i), .in15(ALUSel_and_i), .out(ALUSel_I), .sel({i[4], i[14:12]}));  // open: in0, in1, in2, in3, in4, in5, in6, in7, in11

  // Other names for the same wires on the sheet: i_opcode[6:0] = i[6:0]; ISel[3:0] = {i[4], i[14:12]};
  //   i_funct3[2:0] = i[14:12]; i_funct7[6:0] = i[31:25]; b_four_b[3:0] = INSTRUCTION[3:0];
  //   t_four_b[3:0] = INSTRUCTION[6:3]; first_b = INSTRUCTION[6]; r_func7[6:0] = r[31:25];
  //   RSel[4:0] = {r[14:12], r[30], r[25]}; r_func3[2:0] = r[14:12]; sb_funct3[2:0] = sb[14:12]
endmodule

module ImmGen (
  input  [31:0] instruction,
  input  [2:0] ImmSel,
  output [31:0] immediate
);

  wire [4:0] demultiplexer_1_out3;
  wire [24:0] demultiplexer_1_out0, demultiplexer_1_out4;
  wire [24:5] demultiplexer_1_out1, demultiplexer_1_out2;
  wire [31:0] imm_gen_i, imm_gen_s;
  wire [31:1] imm_gen_sb, imm_gen_uj;
  wire [31:12] imm_gen_u;

  Demultiplexer #(.select(3), .width(25), .enable("false")) demultiplexer_1 (
    .out0({demultiplexer_1_out0[24], imm_gen_i[10:0], demultiplexer_1_out0[12:0]}),
    .out1({demultiplexer_1_out1[24], imm_gen_s[10:5], demultiplexer_1_out1[17:5], imm_gen_s[4:0]}),
    .out2({demultiplexer_1_out2[24], imm_gen_sb[10:5], demultiplexer_1_out2[17:5], imm_gen_sb[4:1], imm_gen_sb[11]}),
    .out3({imm_gen_u, demultiplexer_1_out3}),
    .out4({demultiplexer_1_out4[24], imm_gen_uj[10:1], imm_gen_uj[11], imm_gen_uj[19:12], demultiplexer_1_out4[4:0]}),
    .in(instruction[31:7]), .sel(ImmSel));  // open: out5, out6, out7
  assign imm_gen_i[31:11] = {{20{demultiplexer_1_out0[24]}}, demultiplexer_1_out0[24]};  // Bit_Extender bit_extender_1
  assign imm_gen_s[31:11] = {{20{demultiplexer_1_out1[24]}}, demultiplexer_1_out1[24]};  // Bit_Extender bit_extender_2
  assign imm_gen_uj[31:20] = {{11{demultiplexer_1_out4[24]}}, demultiplexer_1_out4[24]};  // Bit_Extender bit_extender_3
  assign imm_gen_sb[31:12] = {{19{demultiplexer_1_out2[24]}}, demultiplexer_1_out2[24]};  // Bit_Extender bit_extender_4
  Multiplexer #(.select(3), .width(32), .enable("false")) multiplexer_1 (
    .in0(imm_gen_i), .in1(imm_gen_s), .in2({imm_gen_sb, 1'b0}), .in3({imm_gen_u, {12{1'b0}}}),
    .in4({imm_gen_uj, 1'b0}), .out(immediate), .sel(ImmSel));  // open: in5, in6, in7
endmodule

module BranchComp (
  input  [31:0] rs1,
  input  [31:0] rs2,
  input  BrUn,
  output BrEq,
  output BrLT
);

  wire BrEq_signed, BrEq_unsigned, BrLT_signed, BrLT_unsigned;

  Multiplexer #(.enable("false")) multiplexer_1 (.in0(BrEq_signed), .in1(BrEq_unsigned), .out(BrEq), .sel(BrUn));
  Comparator #(.width(32)) comparator_1 (.a(rs1), .b(rs2), .eq(BrEq_signed), .lt(BrLT_signed));  // open: gt
  Comparator #(.width(32), .mode("unsigned")) comparator_2 (
    .a(rs1), .b(rs2), .eq(BrEq_unsigned), .lt(BrLT_unsigned));  // open: gt
  Multiplexer #(.enable("false")) multiplexer_2 (.in0(BrLT_signed), .in1(BrLT_unsigned), .out(BrLT), .sel(BrUn));
endmodule

module Instruction_Mem (
  input  [31:0] INSTRUCTION,
  output [4:0] rs1,
  output [4:0] rd,
  output [4:0] rs2
);

  wire [3:0] form_sel;
  wire [4:0] i_load_rd, i_load_rs1, multiplexer_4_out, uj_rs1;
  wire [31:0] i, i_loads, jalr, r, r_or_u, s, sb, u, uj;

  Multiplexer #(.width(4), .enable("false")) multiplexer_1 (
    .in0(INSTRUCTION[6:3]), .in1(INSTRUCTION[3:0]), .out(form_sel), .sel(INSTRUCTION[6]));
  Multiplexer #(.select(4), .width(5), .enable("false")) multiplexer_2 (
    .in0(i_load_rs1), .in2(i[19:15]), .in3(sb[19:15]), .in4(s[19:15]), .in6(r[19:15]), .in7(jalr[19:15]),
    .in15(uj_rs1), .out(rs1), .sel(form_sel));  // open: in1, in5, in8, in9, in10, in11, in12, in13, in14
  Demultiplexer #(.select(4), .width(32), .enable("false")) demultiplexer_1 (
    .out0({i_loads[31:20], i_load_rs1, i_loads[14:12], i_load_rd, i_loads[6:0]}), .out2(i), .out3(sb),
    .out4(s), .out6(r_or_u), .out7(jalr), .out15(uj), .in(INSTRUCTION), .sel(form_sel));  // open: out1, out5, out8, out9, out10, out11, out12, out13, out14
  Multiplexer #(.select(4), .width(5), .enable("false")) multiplexer_3 (
    .in3(sb[24:20]), .in4(s[24:20]), .in6(r[24:20]), .out(rs2), .sel(form_sel));  // open: in0, in1, in2, in5, in7, in8, in9, in10, in11, in12, in13, in14, in15
  Multiplexer #(.select(4), .width(5), .enable("false")) multiplexer_4 (
    .in3(r[11:7]), .in7(u[11:7]), .out(multiplexer_4_out), .sel(INSTRUCTION[3:0]));  // open: in0, in1, in2, in4, in5, in6, in8, in9, in10, in11, in12, in13, in14, in15
  Demultiplexer #(.select(4), .width(32), .enable("false")) demultiplexer_2 (
    .out3(r), .out7(u), .in(r_or_u), .sel(INSTRUCTION[3:0]));  // open: out0, out1, out2, out4, out5, out6, out8, out9, out10, out11, out12, out13, out14, out15
  Multiplexer #(.select(4), .width(5), .enable("false")) multiplexer_5 (
    .in0(i_load_rd), .in2(i[11:7]), .in6(multiplexer_4_out), .in7(jalr[11:7]), .in15(uj[11:7]), .out(rd),
    .sel(form_sel));  // open: in1, in3, in4, in5, in8, in9, in10, in11, in12, in13, in14

  // Other names for the same wires on the sheet: i_rd[4:0] = i[11:7]; i_rs1[4:0] = i[19:15];
  //   i_loads (some bits) = {i_load_rs1, i_load_rd}; b_four_b[3:0] = INSTRUCTION[3:0];
  //   t_four_b[3:0] = INSTRUCTION[6:3]; first_b = INSTRUCTION[6]; jalr_rd[4:0] = jalr[11:7];
  //   jalr_rs1[4:0] = jalr[19:15]; r_rd[4:0] = r[11:7]; r_rs1[4:0] = r[19:15]; r_rs2[4:0] = r[24:20];
  //   s_rs1[4:0] = s[19:15]; s_rs2[4:0] = s[24:20]; sb_rs1[4:0] = sb[19:15]; sb_rs2[4:0] = sb[24:20];
  //   u_rd[4:0] = u[11:7]; uj_rd[4:0] = uj[11:7]
endmodule
